# Fritzing sketch locus-final-new (saved by Fritzing 0.9.3b)
circuit board: 12.3059cm x 7.50047cm
breadboards: 1

parts:
  10k = Resistor [tolerance=±5% resistance=1k package=THT]
  10k_2 = Resistor [tolerance=±5% resistance=1k package=THT]
  U1 = ESP-12F (ESP8266 WiFi Module) [part_number=ESP8266]
  IC1 = Voltage Regulator AMS1117 [package=sot223]
  +_- = female pin header, 2 pins [form="♀ (female)"]
  C1 = Electrolytic Capacitor [capacitance=1µF package="100 mil [THT, electrolytic]"]
  C2 = Electrolytic Capacitor [capacitance=1µF package="100 mil [THT, electrolytic]"]
  10k_3 = Resistor [tolerance=±5% resistance=1k package=THT]
  DHT1 = DHT11 Humitidy and Temperature Sensor
  4k7 = Resistor [tolerance=±5% resistance=220 package=THT]
  relay2 = songle relay
  Q1 = NPN-Transistor [package="TO92 [THT]"]
  10k_4 = Resistor [tolerance=±5% resistance=220 package=THT]
  D1 = Rectifier Diode [part_number=1N4001 package="300 mil [THT]"]
  Scale_1 = HX711 Weighing Sensor Module
  scale_2 = HX711 Weighing Sensor Module
  J2 = screw terminal, 3 pins

nets:
  N1: 10k.Pin_0, U1.GPIO15
  GND: 10k.Pin_1, IC1.GND, +_-.pin1, C1.-, C2.-, DHT1.GND, Q1.E, Scale_1.GND, scale_2.GND
  VCC: 10k_2.Pin_0, U1.VCC, IC1.OUT, C1.+, 10k_3.Pin_0, DHT1.VDD, 4k7.Pin_0, Scale_1.VCC, scale_2.VCC
  N2: 10k_2.Pin_1, U1.EN
  N3: U1.GPIO4, scale_2.CK/TX
  N4: U1.GPIO5, scale_2.DO/RX
  N5: U1.GPIO16, 10k_4.Pin_1
  N6: U1.GPIO14, DHT1.DATA, 4k7.Pin_1
  N7: U1.GPIO12, Scale_1.DO/RX
  N8: U1.GPIO13, Scale_1.CK/TX
  N9: U1.RST, 10k_3.Pin_1
  N10: IC1.IN, +_-.pin2, C2.+, relay2.GND, D1.cathode
  N11: relay2.VCC, Q1.C, D1.anode
  N12: relay2.NO, J2.pin3
  N13: relay2.NC, J2.pin1
  N14: relay2.COMMON, J2.pin2
  N15: Q1.B, 10k_4.Pin_0

custom parts:
  ESP-12F (ESP8266 WiFi Module): WiFi Module based on the ESP8266 with onboard PCB antenna and UART communications
  DHT11 Humitidy and Temperature Sensor: DHT11 Humidity and Temperature Sensor
